# Fritzing sketch 2 (saved by Fritzing 0.9.3b)

parts:
  Part1 = Solar Panel [package="Renogy 50 Watts 12 Volt Monocrystalline Bendable Solar Panel"]
  A1 = CN3065 Mini Solar Charger Module
  BAT1 = 18650 battery holder [package=battery-18650-kit]
  BAT2 = 18650 battery holder [package=battery-18650-kit]
  A2 = 18650 to dual USB boost module

nets:
  N1: Part1.Connector_1, A1.Pin_1, A1.Pin_3
  N2: Part1.Connector_2, A1.Pin_2, A1.Pin_4, A1.Pin_12, BAT2.-
  N3: A1.Pin_11, BAT1.+, BAT2.+, A2.Pin_1
  N4: BAT1.-, A2.Pin_2

custom parts:
  Solar Panel: Renogy 50 Watts 12 Volt Solar Panel
  CN3065 Mini Solar Charger Module: CN3791 MPPT Solar Panel Regulator Controller 6V 9V 12V 1 Zelle Lithium-Batterie Ladung Solar Panel Ladegerät board-Controller Module.
  18650 battery holder: 18650 Battery Holder identical to the dual battery version.
  18650 to dual USB boost module: 18650 to dual USB boost module.
